# Fritzing sketch BikeSonar (saved by Fritzing 0.9.3b)
breadboards: 1

parts:
  Digispark1 = Digispark
  J1 = Piezo Speaker
  hc-sr1 = hc-sr04
  S1 = Toggle Switch [package=THT]
  VCC1 = Battery block 9V

nets:
  VCC: Digispark1.VCC, hc-sr1.VCC
  GND: Digispark1.GND, J1.pin1, hc-sr1.GND, VCC1.-
  N1: Digispark1.VIN, S1.L1
  N2: Digispark1.P0, hc-sr1.Trig
  N3: Digispark1.P1, hc-sr1.Echo
  N4: Digispark1.P2, J1.pin2
  N5: S1.COM, VCC1.+

custom parts:
  Digispark: The Digispark is an Attiny85 based microcontroller development board similar to the Arduino line, only cheaper, smaller, and a bit less powerful. With a whole host of shields to extend its functionality and the ability to use the familiar Arduino IDE the Digispark is a great way to jump into electronics, or perfect for when an Arduino is too big or too much.
